# Fritzing sketch scheme (saved by Fritzing 0.9.3b)
breadboards: 2

parts:
  M1 = STM32F103C8T6 blue mini board
  LED1 = smd LED [color="Red (633nm)" package="0603 [SMD]"]
  R1 = Resistor [tolerance=±5% resistance=220 package=THT]
  R2 = PHOTOCELL [package=photocell-kit]
  R3 = Resistor [tolerance=±5% resistance=1k package=THT]

nets:
  N1: M1.G, M1.B11, M1.GND
  N2: M1.3.3V, M1.B1
  N3: M1.A4, LED1.anode
  N4: M1.B10, M1.connector45, M1.Boot0
  N5: LED1.cathode, R1.Pin_1
  N6: R1.Pin_0, R3.Pin_0
  N7: R2.P$1, R3.Pin_1

custom parts:
  STM32F103C8T6 blue mini board: Generic Blue Pill microcomputer module, available from Ebay and others. CPU STM32F103C8 72Mhz Flash: 64 KB/128 KB RAM: 20KB.
