# Fritzing sketch scheme (saved by Fritzing 0.9.3b)
breadboards: 1

parts:
  M1 = STM32F103C8T6 blue mini board
  LED1 = LED - 3mm [color="Red (633nm)" package="3 mm [THT]"]
  R1 = Resistor [tolerance=±0.5% resistance=450 package="0402 [SMD]"]
  Part1 = Adafruit MCP4725 Breakout Board - 12-Bit DAC [part_number="Adafruit #935"]

nets:
  GND: M1.G, M1.B11, M1.GND, R1.Pin_0, Part1.GND, Part1.SDA
  3.3V: M1.3.3V, M1.B1, Part1.VDD
  N1: M1.B10, M1.connector45, M1.Boot0, Part1.SCL
  N2: LED1.cathode, R1.Pin_1
  N3: LED1.anode, Part1.VOUT

custom parts:
  STM32F103C8T6 blue mini board: Generic Blue Pill microcomputer module, available from Ebay and others. CPU STM32F103C8 72Mhz Flash: 64 KB/128 KB RAM: 20KB.
  Adafruit MCP4725 Breakout Board - 12-Bit DAC: Your microcontroller probably has an ADC (analog -> digital converter) but does it have a DAC (digital -> analog converter)??? Now it can! This breakout board features the easy-to-use MCP4725 12-bit DAC. Control it via I2C and send it the value you want it to output, and the VOUT pin will have it. Great for audio / analog projects, such as when you can't use PWM but need a sine wave or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
