# Fritzing sketch scheme (saved by Fritzing 0.9.3b)
breadboards: 1

parts:
  M1 = STM32F103C8T6 blue mini board
  LED1 = smd LED [color="Red (633nm)" package="0805 [SMD]"]
  R1 = Resistor [tolerance=±5% resistance=220 package=THT]
  R2 = Resistor [tolerance=±5% resistance=220 package=THT]
  S1 = Pushbutton [package="[SMD]"]

nets:
  N1: M1.G, M1.B11, M1.GND, LED1.cathode, R2.Pin_1
  N2: M1.3.3V, M1.B1, M1.3.3, S1.Pin_1, S1.Pin_2
  N3: M1.A4, R2.Pin_0, S1.Pin_3, S1.Pin_4
  N4: M1.B10, M1.connector45, M1.Boot0
  N5: LED1.anode, R1.Pin_0

custom parts:
  STM32F103C8T6 blue mini board: Generic Blue Pill microcomputer module, available from Ebay and others. CPU STM32F103C8 72Mhz Flash: 64 KB/128 KB RAM: 20KB.
