# Fritzing sketch scheme (saved by Fritzing 0.9.3b)
breadboards: 1

parts:
  M1 = STM32F103C8T6 blue mini board
  Part2 = Adafruit BMP280 [part_number="Adafruit #2651"]

nets:
  GND: M1.G, M1.B11, M1.GND, Part2.GND, Part2.SDI/SDA
  N1: M1.3.3V, M1.B1
  N2: M1.B10, M1.connector45, M1.Boot0

custom parts:
  STM32F103C8T6 blue mini board: Generic Blue Pill microcomputer module, available from Ebay and others. CPU STM32F103C8 72Mhz Flash: 64 KB/128 KB RAM: 20KB.
  Adafruit BMP280: Bosch has stepped up their game with their new BMP280 sensor, an environmental sensor with temperature, barometric pressure that is the next generation upgrade to the BMP085/BMP180/BMP183. This sensor is great for all sorts of weather sensing and can even be used in both I2C and SPI! This precision sensor from Bosch is the best low-cost, precision sensing solution for measuring barometric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
