# Fritzing sketch scheme (saved by Fritzing 0.9.3b)
breadboards: 1

parts:
  M1 = STM32F103C8T6 blue mini board

nets:
  N1: M1.G, M1.B11, M1.GND
  N2: M1.3.3V, M1.B1
  N3: M1.B10, M1.connector45, M1.Boot0

custom parts:
  STM32F103C8T6 blue mini board: Generic Blue Pill microcomputer module, available from Ebay and others. CPU STM32F103C8 72Mhz Flash: 64 KB/128 KB RAM: 20KB.
